// Logisim project 1.circ as structural Verilog: 3 circuits, main circuit main
module main (
  input  in_1,
  input  in_2,
  output out_3,
  output out_4
);

  // _1 1_1: pin names not known; wires that end beside it: in_1, in_2, out_3, out_4
endmodule

module _1 (
  input  in_1,
  input  in_2,
  output out_3,
  output out_4,
  output out_5,
  output out_6
);

  wire not_1_out, not_2_out;

  not not_1 (not_1_out, in_1);
  not not_2 (not_2_out, in_2);
  and and_1 (out_3, not_1_out, not_2_out);
  and and_2 (out_4, in_1, not_2_out);
  and and_3 (out_5, not_1_out, in_2);
  and and_4 (out_6, in_2, in_1);
endmodule

module _2 (
  input  in_1,
  input  in_2,
  input  in_3,
  input  in_4
);

  wire and_1_out, and_2_out, and_3_out, and_4_out, undriven, undriven_2, undriven_3, undriven_4;

  and and_1 (and_1_out, in_1, undriven_4);
  and and_2 (and_2_out, in_2, undriven_3);
  and and_3 (and_3_out, in_3, undriven_2);
  and and_4 (and_4_out, in_4, undriven);
  // OR_Gate or_1 has open pins: in0=and_1_out, in1=and_2_out, in2=and_3_out, in3=and_4_out, out=open
endmodule
